# Fritzing sketch Piezo Module (saved by Fritzing 0.6.3b)
breadboards: 1

parts:
  Nano1 = Arduino Nano v2.3
  R1 = Resistor [tolerance=±5% resistance=330 package="0603 [SMD]"]
  R2 = Resistor [tolerance=±5% resistance=100 package="0603 [SMD]"]
  Part1 = Gadgeteer_Extender_Module
  R3 = Resistor [tolerance=±5% resistance=100 package="0603 [SMD]"]
  R4 = Resistor [tolerance=±5% resistance=330 package="0603 [SMD]"]
  R5 = Resistor [tolerance=±5% resistance=10k package="0603 [SMD]"]
  R6 = Resistor [tolerance=±5% resistance=10k package="0603 [SMD]"]
  J1 = female pin header, 1 pin [form="♀ (female)"]
  R7 = Resistor [tolerance=±5% resistance=10k package="0603 [SMD]"]
  R8 = Resistor [tolerance=±5% resistance=10k package="0603 [SMD]"]
  R9 = Resistor [tolerance=±5% resistance=330 package="0603 [SMD]"]
  R10 = Resistor [tolerance=±5% resistance=330 package="0603 [SMD]"]
  R11 = Resistor [tolerance=±5% resistance=100 package="0603 [SMD]"]
  R12 = Resistor [tolerance=±5% resistance=100 package="0603 [SMD]"]

nets:
  N1: Nano1.RST, Part1.connector9, R7.Pin_0, R8.Pin_0
  N2: Nano1.GND, R2.Pin_0
  N3: Nano1.D2, R3.Pin_1
  N4: Nano1.A4, R5.Pin_1
  N5: Nano1.A3, R6.Pin_1
  N6: Nano1.VIN, R1.Pin_0, Part1.connector1, Part1.connector8, R4.Pin_0, J1.pin1, R9.Pin_0, R10.Pin_0
  N7: R1.Pin_1, R2.Pin_1, Part1.connector7, R6.Pin_0
  N8: Part1.connector6, R3.Pin_0, R4.Pin_1, R5.Pin_0
  N9: R7.Pin_1, R9.Pin_1, R11.Pin_1
  N10: R8.Pin_1, R10.Pin_1, R12.Pin_0

notes:
  P3 = Neighborhood Bus (upstream)
  P4 = SDA
  P5 = SCL
  Xtra = 3* = Neighborhood Bus (downstream)
